# Fritzing sketch LEDMatrix (saved by Fritzing 0.8.7b)
breadboards: 1

parts:
  Bauteil1 = Arduino Board Ethernet
  LED1 = LED - 5mm [color="Red (633nm)" package="5 mm [THT]"]
  LED2 = LED - 5mm [color="Red (633nm)" package="5 mm [THT]"]
  LED3 = LED - 5mm [color="Red (633nm)" package="5 mm [THT]"]
  LED4 = LED - 5mm [color="Red (633nm)" package="5 mm [THT]"]
  LED5 = LED - 5mm [color="Red (633nm)" package="5 mm [THT]"]
  LED6 = LED - 5mm [color="Red (633nm)" package="5 mm [THT]"]
  R1 = Resistor [tolerance=±5% resistance=220 package=THT]

nets:
  N1: Bauteil1.D8, LED6.anode
  N2: Bauteil1.D2_PWM, LED1.anode
  N3: Bauteil1.D3_PWM, LED2.anode
  N4: Bauteil1.D5_PWM, LED3.anode
  N5: Bauteil1.D6_PWM, LED4.anode
  N6: Bauteil1.D7, LED5.anode
  N7: Bauteil1.GND, R1.Pin_1
  N8: LED1.cathode, LED2.cathode, LED3.cathode, LED4.cathode, LED5.cathode, LED6.cathode, R1.Pin_0
